// Logisim project project.circ as structural Verilog
module asset_memory (
  input  [7:0] addr,
  input  clock,
  output [11:0] column,
  output \end 
);

  wire [2:0] multiplexer_1_out;
  wire [3:0] counter_1_q, undriven;
  wire [11:0] multiplexer_3_out, multiplexer_4_out, multiplexer_5_out, multiplexer_6_out, multiplexer_7_out,
       multiplexer_8_out, multiplexer_9_out, multiplexer_10_out, multiplexer_11_out, multiplexer_12_out,
       multiplexer_13_out, multiplexer_14_out, multiplexer_15_out, multiplexer_16_out, multiplexer_17_out,
       multiplexer_18_out;

  Counter #(.width(4), .max('hf)) counter_1 (.Q(counter_1_q), .carry(\end ), .clk(clock));  // open: load, D, count, clr
  DotMatrix #(.matrixcols(12), .matrixrows(12)) dotmatrix_1 (
    .col0({12{1'b0}}), .col1({12{1'b0}}), .col2({12{1'b0}}), .col3({12{1'b0}}), .col4({12{1'b0}}),
    .col5({12{1'b0}}), .col6({12{1'b0}}), .col7({12{1'b0}}), .col8({12{1'b0}}), .col9({12{1'b0}}),
    .col10({12{1'b0}}), .col11({12{1'b0}}));
  DotMatrix #(.matrixcols(12), .matrixrows(12)) dotmatrix_2 (
    .col0({12{1'b0}}), .col1({12{1'b0}}), .col2({12{1'b0}}), .col3(12'h2), .col4(12'h30e), .col5(12'h7be),
    .col6(12'h7be), .col7(12'h30e), .col8(12'h2), .col9({12{1'b0}}), .col10({12{1'b0}}), .col11({12{1'b0}}));
  DotMatrix #(.matrixcols(12), .matrixrows(12)) dotmatrix_3 (
    .col0({12{1'b0}}), .col1({12{1'b0}}), .col2(12'hc0), .col3(12'h1c2), .col4(12'h86), .col5(12'h396),
    .col6(12'h7f6), .col7(12'h3f6), .col8(12'h1e2), .col9({12{1'b0}}), .col10({12{1'b0}}), .col11({12{1'b0}}));
  DotMatrix #(.matrixcols(12), .matrixrows(12)) dotmatrix_4 (
    .col0({12{1'b0}}), .col1({12{1'b0}}), .col2(12'h2), .col3(12'ha), .col4(12'h31a), .col5(12'h6fa),
    .col6(12'h5fa), .col7(12'h31a), .col8(12'ha), .col9(12'h2), .col10({12{1'b0}}), .col11({12{1'b0}}));
  Multiplexer #(.select(4), .width(3)) multiplexer_1 (
    .in0(3'b000), .in1(3'b000), .in2(3'b000), .in3(3'b000), .in4(3'b000), .in5(3'b000), .in6(3'b011),
    .in7(3'b000), .in8(3'b110), .in9(3'b000), .in10(3'b000), .in11(3'b101), .in12(3'b000), .in13(3'b100),
    .in14(3'b010), .in15(3'b001), .out(multiplexer_1_out), .sel(addr[3:0]));  // open: en
  Multiplexer #(.select(3), .width(12), .enable("false")) multiplexer_2 (
    .in0(multiplexer_3_out), .in1(multiplexer_4_out), .in2(multiplexer_5_out), .in3(multiplexer_6_out),
    .in4(multiplexer_10_out), .in5(multiplexer_9_out), .in6(multiplexer_8_out), .in7(multiplexer_7_out),
    .out(column), .sel(multiplexer_1_out));
  Multiplexer #(.select(4), .width(12), .enable("false")) multiplexer_3 (
    .in0({12{1'b0}}), .in1({12{1'b0}}), .in2({12{1'b0}}), .in3({12{1'b0}}), .in4({12{1'b0}}),
    .in5({12{1'b0}}), .in6({12{1'b0}}), .in7({12{1'b0}}), .in8({12{1'b0}}), .in9({12{1'b0}}),
    .in10({12{1'b0}}), .in11({12{1'b0}}), .out(multiplexer_3_out), .sel(counter_1_q));  // open: in12, in13, in14, in15
  Multiplexer #(.select(4), .width(12), .enable("false")) multiplexer_4 (
    .in0({12{1'b0}}), .in1({12{1'b0}}), .in2({12{1'b0}}), .in3(12'h2), .in4(12'h30e), .in5(12'h7be),
    .in6(12'h7be), .in7(12'h30e), .in8(12'h2), .in9({12{1'b0}}), .in10({12{1'b0}}), .in11({12{1'b0}}),
    .out(multiplexer_4_out), .sel(counter_1_q));  // open: in12, in13, in14, in15
  Multiplexer #(.select(4), .width(12), .enable("false")) multiplexer_5 (
    .in0({12{1'b0}}), .in1({12{1'b0}}), .in2(12'hc0), .in3(12'h1c2), .in4(12'h86), .in5(12'h396),
    .in6(12'h7f6), .in7(12'h3f6), .in8(12'h1e2), .in9({12{1'b0}}), .in10({12{1'b0}}), .in11({12{1'b0}}),
    .out(multiplexer_5_out), .sel(counter_1_q));  // open: in12, in13, in14, in15
  Multiplexer #(.select(4), .width(12), .enable("false")) multiplexer_6 (
    .in0({12{1'b0}}), .in1({12{1'b0}}), .in2(12'h2), .in3(12'ha), .in4(12'h31a), .in5(12'h6fa),
    .in6(12'h5fa), .in7(12'h31a), .in8(12'ha), .in9(12'h2), .in10({12{1'b0}}), .in11({12{1'b0}}),
    .out(multiplexer_6_out), .sel(counter_1_q));  // open: in12, in13, in14, in15
  Multiplexer #(.select(4), .width(12), .enable("false")) multiplexer_7 (
    .in0({12{1'b0}}), .in1({12{1'b0}}), .in2({12{1'b0}}), .in3(12'h180), .in4(12'h1b8), .in5(12'h70),
    .in6(12'h70), .in7(12'h1b8), .in8(12'h180), .in9({12{1'b0}}), .in10({12{1'b0}}), .in11({12{1'b0}}),
    .out(multiplexer_7_out), .sel(counter_1_q));  // open: in12, in13, in14, in15
  Multiplexer #(.select(4), .width(12), .enable("false")) multiplexer_8 (
    .in0({12{1'b0}}), .in1({12{1'b0}}), .in2(12'he0), .in3(12'h72), .in4(12'hfa), .in5(12'h5fa),
    .in6(12'h5fa), .in7(12'hfa), .in8(12'h72), .in9(12'he0), .in10({12{1'b0}}), .in11({12{1'b0}}),
    .out(multiplexer_8_out), .sel(counter_1_q));  // open: in12, in13, in14, in15
  Multiplexer #(.select(4), .width(12), .enable("false")) multiplexer_9 (
    .in0({12{1'b0}}), .in1(12'h1e0), .in2(12'h1b0), .in3(12'h15a), .in4(12'h9a), .in5(12'h7fa),
    .in6(12'h7fa), .in7(12'h9a), .in8(12'h15a), .in9(12'h1b0), .in10(12'h1e0), .in11({12{1'b0}}),
    .out(multiplexer_9_out), .sel(counter_1_q));  // open: in12, in13, in14, in15
  Multiplexer #(.select(4), .width(12), .enable("false")) multiplexer_10 (
    .in0({12{1'b0}}), .in1({12{1'b0}}), .in2(12'h2), .in3(12'h60a), .in4(12'h2fa), .in5(12'h6fa),
    .in6(12'h6fa), .in7(12'h2fa), .in8(12'h60a), .in9(12'h2), .in10({12{1'b0}}), .in11({12{1'b0}}),
    .out(multiplexer_10_out), .sel(counter_1_q));  // open: in12, in13, in14, in15
  DotMatrix #(.matrixcols(12), .matrixrows(12)) dotmatrix_5 (
    .col0({12{1'b0}}), .col1({12{1'b0}}), .col2({12{1'b0}}), .col3(12'h180), .col4(12'h1b8), .col5(12'h70),
    .col6(12'h70), .col7(12'h1b8), .col8(12'h180), .col9({12{1'b0}}), .col10({12{1'b0}}), .col11({12{1'b0}}));
  DotMatrix #(.matrixcols(12), .matrixrows(12)) dotmatrix_6 (
    .col0({12{1'b0}}), .col1({12{1'b0}}), .col2(12'he0), .col3(12'h72), .col4(12'hfa), .col5(12'h5fa),
    .col6(12'h5fa), .col7(12'hfa), .col8(12'h72), .col9(12'he0), .col10({12{1'b0}}), .col11({12{1'b0}}));
  DotMatrix #(.matrixcols(12), .matrixrows(12)) dotmatrix_7 (
    .col0({12{1'b0}}), .col1(12'h1e0), .col2(12'h1b0), .col3(12'h15a), .col4(12'h9a), .col5(12'h7fa),
    .col6(12'h7fa), .col7(12'h9a), .col8(12'h15a), .col9(12'h1b0), .col10(12'h1e0), .col11({12{1'b0}}));
  DotMatrix #(.matrixcols(12), .matrixrows(12)) dotmatrix_8 (
    .col0({12{1'b0}}), .col1({12{1'b0}}), .col2(12'h2), .col3(12'h60a), .col4(12'h2fa), .col5(12'h6fa),
    .col6(12'h6fa), .col7(12'h2fa), .col8(12'h60a), .col9(12'h2), .col10({12{1'b0}}), .col11({12{1'b0}}));
  DotMatrix #(.matrixcols(12), .matrixrows(12)) dotmatrix_9 (
    .col0({12{1'b0}}), .col1({12{1'b0}}), .col2({12{1'b0}}), .col3({12{1'b0}}), .col4({12{1'b0}}),
    .col5({12{1'b0}}), .col6({12{1'b0}}), .col7({12{1'b0}}), .col8({12{1'b0}}), .col9({12{1'b0}}),
    .col10({12{1'b0}}), .col11({12{1'b0}}));
  DotMatrix #(.matrixcols(12), .matrixrows(12)) dotmatrix_10 (
    .col0({12{1'b0}}), .col1({12{1'b0}}), .col2(12'h3), .col3(12'h30d), .col4(12'h4b1), .col5(12'h841),
    .col6(12'h841), .col7(12'h4b1), .col8(12'h30d), .col9(12'h3), .col10({12{1'b0}}), .col11({12{1'b0}}));
  DotMatrix #(.matrixcols(12), .matrixrows(12)) dotmatrix_11 (
    .col0({12{1'b0}}), .col1(12'hc0), .col2(12'h123), .col3(12'h225), .col4(12'h359), .col5(12'hc69),
    .col6(12'h809), .col7(12'h409), .col8(12'h21d), .col9(12'h1e3), .col10({12{1'b0}}), .col11({12{1'b0}}));
  DotMatrix #(.matrixcols(12), .matrixrows(12)) dotmatrix_12 (
    .col0({12{1'b0}}), .col1(12'h3), .col2(12'hd), .col3(12'h395), .col4(12'h4e5), .col5(12'h905),
    .col6(12'ha05), .col7(12'hce5), .col8(12'h395), .col9(12'hd), .col10(12'h3), .col11({12{1'b0}}));
  Multiplexer #(.select(4), .width(12), .enable("false")) multiplexer_11 (
    .in0({12{1'b0}}), .in1({12{1'b0}}), .in2({12{1'b0}}), .in3({12{1'b0}}), .in4({12{1'b0}}),
    .in5({12{1'b0}}), .in6({12{1'b0}}), .in7({12{1'b0}}), .in8({12{1'b0}}), .in9({12{1'b0}}),
    .in10({12{1'b0}}), .in11({12{1'b0}}), .out(multiplexer_11_out), .sel(undriven));  // open: in12, in13, in14, in15
  Multiplexer #(.select(4), .width(12), .enable("false")) multiplexer_12 (
    .in0({12{1'b0}}), .in1({12{1'b0}}), .in2(12'h3), .in3(12'h30d), .in4(12'h4b1), .in5(12'h841),
    .in6(12'h841), .in7(12'h4b1), .in8(12'h30d), .in9(12'h3), .in10({12{1'b0}}), .in11({12{1'b0}}),
    .out(multiplexer_12_out), .sel(undriven));  // open: in12, in13, in14, in15
  Multiplexer #(.select(4), .width(12), .enable("false")) multiplexer_13 (
    .in0({12{1'b0}}), .in1(12'hc0), .in2(12'h123), .in3(12'h225), .in4(12'h359), .in5(12'hc69),
    .in6(12'h809), .in7(12'h409), .in8(12'h21d), .in9(12'h1e3), .in10({12{1'b0}}), .in11({12{1'b0}}),
    .out(multiplexer_13_out), .sel(undriven));  // open: in12, in13, in14, in15
  Multiplexer #(.select(4), .width(12), .enable("false")) multiplexer_14 (
    .in0({12{1'b0}}), .in1(12'h3), .in2(12'hd), .in3(12'h395), .in4(12'h4e5), .in5(12'h905), .in6(12'ha05),
    .in7(12'hce5), .in8(12'h395), .in9(12'hd), .in10(12'h3), .in11({12{1'b0}}), .out(multiplexer_14_out),
    .sel(undriven));  // open: in12, in13, in14, in15
  DotMatrix #(.matrixcols(12), .matrixrows(12)) dotmatrix_13 (
    .col0({12{1'b0}}), .col1({12{1'b0}}), .col2(12'h3fc), .col3(12'h27c), .col4(12'h244), .col5(12'h38c),
    .col6(12'h38c), .col7(12'h244), .col8(12'h27c), .col9(12'h3fc), .col10({12{1'b0}}), .col11({12{1'b0}}));
  Multiplexer #(.select(4), .width(12), .enable("false")) multiplexer_15 (
    .in0({12{1'b0}}), .in1({12{1'b0}}), .in2(12'h3fc), .in3(12'h27c), .in4(12'h244), .in5(12'h38c),
    .in6(12'h38c), .in7(12'h244), .in8(12'h27c), .in9(12'h3fc), .in10({12{1'b0}}), .in11({12{1'b0}}),
    .out(multiplexer_15_out), .sel(undriven));  // open: in12, in13, in14, in15
  DotMatrix #(.matrixcols(12), .matrixrows(12)) dotmatrix_14 (
    .col0({12{1'b0}}), .col1({12{1'b0}}), .col2(12'he0), .col3(12'h72), .col4(12'hfa), .col5(12'h5fa),
    .col6(12'h5fa), .col7(12'hfa), .col8(12'h72), .col9(12'he0), .col10({12{1'b0}}), .col11({12{1'b0}}));
  Multiplexer #(.select(4), .width(12), .enable("false")) multiplexer_16 (
    .in0({12{1'b0}}), .in1({12{1'b0}}), .in2(12'he0), .in3(12'h72), .in4(12'hfa), .in5(12'h5fa),
    .in6(12'h5fa), .in7(12'hfa), .in8(12'h72), .in9(12'he0), .in10({12{1'b0}}), .in11({12{1'b0}}),
    .out(multiplexer_16_out), .sel(undriven));  // open: in12, in13, in14, in15
  DotMatrix #(.matrixcols(12), .matrixrows(12)) dotmatrix_15 (
    .col0(12'h1e0), .col1(12'h1e0), .col2(12'h1b0), .col3(12'h15a), .col4(12'h9a), .col5(12'h7fa),
    .col6(12'h7fa), .col7(12'h9a), .col8(12'h15a), .col9(12'h1b0), .col10(12'h1e0), .col11({12{1'b0}}));
  Multiplexer #(.select(4), .width(12), .enable("false")) multiplexer_17 (
    .in0({12{1'b0}}), .in1(12'h1e0), .in2(12'h1b0), .in3(12'h15a), .in4(12'h9a), .in5(12'h7fa),
    .in6(12'h7fa), .in7(12'h9a), .in8(12'h15a), .in9(12'h1b0), .in10(12'h1e0), .in11(12'h1e0),
    .out(multiplexer_17_out), .sel(undriven));  // open: in12, in13, in14, in15
  DotMatrix #(.matrixcols(12), .matrixrows(12)) dotmatrix_16 (
    .col0({12{1'b0}}), .col1(12'h3), .col2(12'he0d), .col3(12'h9f5), .col4(12'h505), .col5(12'h905),
    .col6(12'h905), .col7(12'h505), .col8(12'h9f5), .col9(12'he0d), .col10(12'h3), .col11({12{1'b0}}));
  Multiplexer #(.select(4), .width(12), .enable("false")) multiplexer_18 (
    .in0({12{1'b0}}), .in1(12'h3), .in2(12'he0d), .in3(12'h9f5), .in4(12'h505), .in5(12'h905), .in6(12'h905),
    .in7(12'h505), .in8(12'h9f5), .in9(12'he0d), .in10(12'h3), .in11({12{1'b0}}), .out(multiplexer_18_out),
    .sel(undriven));  // open: in12, in13, in14, in15
endmodule

module matrix16x16 (
  input  [15:0] column,
  input  clk,
  input  res,
  input  [3:0] current_column,
  input  change_matrix,
  output [15:0] column_2,
  output [15:0] column_4,
  output [15:0] column_6,
  output [15:0] column_8,
  output [15:0] column_10,
  output [15:0] column_12,
  output [15:0] column_14,
  output [15:0] column_16,
  output [15:0] column_1,
  output [15:0] column_3,
  output [15:0] column_5,
  output [15:0] column_7,
  output [15:0] column_9,
  output [15:0] column_11,
  output [15:0] column_13,
  output [15:0] column_15
);

  wire controlled_buffer_2_out, decoder_1_out0, decoder_1_out1, decoder_1_out2, decoder_1_out3,
       decoder_1_out4, decoder_1_out5, decoder_1_out6, decoder_1_out7, decoder_1_out8, decoder_1_out9,
       decoder_1_out10, decoder_1_out11, undriven;
  wire [3:0] controlled_buffer_1_out;

  Register #(.width(16)) register_1 (.D(column), .Q(column_1));  // open: en, clk, clr
  Register #(.width(16)) register_2 (.D(column), .Q(column_2));  // open: en, clk, clr
  Register #(.width(16)) register_3 (
    .D(column), .en(decoder_1_out1), .Q(column_4), .clk(clk), .clr(controlled_buffer_2_out));
  Register #(.width(16)) register_4 (
    .D(column), .en(decoder_1_out0), .Q(column_3), .clk(clk), .clr(controlled_buffer_2_out));
  Register #(.width(16)) register_5 (
    .D(column), .en(decoder_1_out2), .Q(column_5), .clk(clk), .clr(controlled_buffer_2_out));
  assign controlled_buffer_1_out = change_matrix ? current_column : 4'bz;  // Controlled_Buffer controlled_buffer_1
  Decoder #(.select(4), .disabled(0)) decoder_1 (
    .out0(decoder_1_out0), .out1(decoder_1_out1), .out2(decoder_1_out2), .out3(decoder_1_out3),
    .out4(decoder_1_out4), .out5(decoder_1_out5), .out6(decoder_1_out6), .out7(decoder_1_out7),
    .out8(decoder_1_out8), .out9(decoder_1_out9), .out10(decoder_1_out10), .out11(decoder_1_out11),
    .sel(controlled_buffer_1_out), .en(change_matrix));  // open: out12, out13, out14, out15
  Register #(.width(16)) register_6 (
    .D(column), .en(decoder_1_out3), .Q(column_6), .clk(clk), .clr(controlled_buffer_2_out));
  Register #(.width(16)) register_7 (
    .D(column), .en(decoder_1_out4), .Q(column_7), .clk(clk), .clr(controlled_buffer_2_out));
  Register #(.width(16)) register_8 (
    .D(column), .en(decoder_1_out5), .Q(column_8), .clk(clk), .clr(controlled_buffer_2_out));
  Register #(.width(16)) register_9 (
    .D(column), .en(decoder_1_out6), .Q(column_9), .clk(clk), .clr(controlled_buffer_2_out));
  Register #(.width(16)) register_10 (
    .D(column), .en(decoder_1_out7), .Q(column_10), .clk(clk), .clr(controlled_buffer_2_out));
  Register #(.width(16)) register_11 (
    .D(column), .en(decoder_1_out8), .Q(column_11), .clk(clk), .clr(controlled_buffer_2_out));
  Register #(.width(16)) register_12 (
    .D(column), .en(decoder_1_out9), .Q(column_12), .clk(clk), .clr(controlled_buffer_2_out));
  Register #(.width(16)) register_13 (
    .D(column), .en(decoder_1_out10), .Q(column_13), .clk(clk), .clr(controlled_buffer_2_out));
  Register #(.width(16)) register_14 (
    .D(column), .en(decoder_1_out11), .Q(column_14), .clk(clk), .clr(controlled_buffer_2_out));
  assign controlled_buffer_2_out = change_matrix ? res : 1'bz;  // Controlled_Buffer controlled_buffer_2
  Register #(.width(16)) register_15 (.D(column), .en(undriven), .Q(column_16));  // open: clk, clr
  Register #(.width(16)) register_16 (.D(column), .Q(column_15));  // open: en, clk, clr

  // Other names for the same wires on the sheet: cng_mtrx = change_matrix
endmodule
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